// Logisim project Common_BUS_8Bit.circ as structural Verilog: 1 circuit, main circuit main
module main (
  input  in_1,
  input  in_2,
  input  in_3,
  input  in_4,
  input  in_5,
  input  in_6,
  input  in_7,
  input  in_8,
  input  in_9,
  input  in_10,
  input  in_11,
  input  in_12,
  input  in_13,
  input  in_14,
  input  in_15,
  input  in_16,
  input  in_17,
  input  in_18,
  input  in_19,
  input  in_20,
  input  in_21,
  input  in_22,
  input  in_23,
  input  in_24,
  input  in_25,
  input  in_26,
  input  in_27,
  input  in_28
);

  wire controlled_buffer_1_out, controlled_buffer_2_out, controlled_buffer_3_out, controlled_buffer_4_out,
       controlled_buffer_5_out, controlled_buffer_6_out, controlled_buffer_7_out, controlled_buffer_8_out,
       d_ff_1_q, d_ff_2_q, d_ff_3_q, d_ff_4_q, d_ff_5_q, d_ff_6_q, d_ff_7_q, d_ff_8_q, d_ff_9_q, d_ff_10_q,
       d_ff_11_q, d_ff_12_q, d_ff_13_q, d_ff_14_q, d_ff_15_q, d_ff_16_q, d_ff_17_q, d_ff_18_q, d_ff_19_q,
       d_ff_20_q, d_ff_21_q, d_ff_22_q, d_ff_23_q, d_ff_24_q;

  D_Flip_Flop d_ff_1 (.D(in_3), .clk(in_1), .Q(d_ff_1_q));  // open: Qn, preset, reset
  D_Flip_Flop d_ff_2 (.D(in_4), .clk(in_1), .Q(d_ff_2_q));  // open: Qn, preset, reset
  D_Flip_Flop d_ff_3 (.D(in_5), .clk(in_1), .Q(d_ff_3_q));  // open: Qn, preset, reset
  D_Flip_Flop d_ff_4 (.D(in_6), .clk(in_1), .Q(d_ff_4_q));  // open: Qn, preset, reset
  D_Flip_Flop d_ff_5 (.D(in_7), .clk(in_1), .Q(d_ff_5_q));  // open: Qn, preset, reset
  D_Flip_Flop d_ff_6 (.D(in_8), .clk(in_1), .Q(d_ff_6_q));  // open: Qn, preset, reset
  D_Flip_Flop d_ff_7 (.D(in_9), .clk(in_1), .Q(d_ff_7_q));  // open: Qn, preset, reset
  D_Flip_Flop d_ff_8 (.D(in_10), .clk(in_1), .Q(d_ff_8_q));  // open: Qn, preset, reset
  D_Flip_Flop d_ff_9 (.D(in_12), .clk(in_1), .Q(d_ff_9_q));  // open: Qn, preset, reset
  D_Flip_Flop d_ff_10 (.D(in_13), .clk(in_1), .Q(d_ff_10_q));  // open: Qn, preset, reset
  D_Flip_Flop d_ff_11 (.D(in_14), .clk(in_1), .Q(d_ff_11_q));  // open: Qn, preset, reset
  D_Flip_Flop d_ff_12 (.D(in_15), .clk(in_1), .Q(d_ff_12_q));  // open: Qn, preset, reset
  D_Flip_Flop d_ff_13 (.D(in_16), .clk(in_1), .Q(d_ff_13_q));  // open: Qn, preset, reset
  D_Flip_Flop d_ff_14 (.D(in_17), .clk(in_1), .Q(d_ff_14_q));  // open: Qn, preset, reset
  D_Flip_Flop d_ff_15 (.D(in_18), .clk(in_1), .Q(d_ff_15_q));  // open: Qn, preset, reset
  D_Flip_Flop d_ff_16 (.D(in_19), .clk(in_1), .Q(d_ff_16_q));  // open: Qn, preset, reset
  D_Flip_Flop d_ff_17 (.D(in_21), .clk(in_1), .Q(d_ff_17_q));  // open: Qn, preset, reset
  D_Flip_Flop d_ff_18 (.D(in_22), .clk(in_1), .Q(d_ff_18_q));  // open: Qn, preset, reset
  D_Flip_Flop d_ff_19 (.D(in_23), .clk(in_1), .Q(d_ff_19_q));  // open: Qn, preset, reset
  D_Flip_Flop d_ff_20 (.D(in_24), .clk(in_1), .Q(d_ff_20_q));  // open: Qn, preset, reset
  D_Flip_Flop d_ff_21 (.D(in_25), .clk(in_1), .Q(d_ff_21_q));  // open: Qn, preset, reset
  D_Flip_Flop d_ff_22 (.D(in_26), .clk(in_1), .Q(d_ff_22_q));  // open: Qn, preset, reset
  D_Flip_Flop d_ff_23 (.D(in_27), .clk(in_1), .Q(d_ff_23_q));  // open: Qn, preset, reset
  D_Flip_Flop d_ff_24 (.D(in_28), .clk(in_1), .Q(d_ff_24_q));  // open: Qn, preset, reset
  assign controlled_buffer_1_out = in_2 ? d_ff_1_q : 1'bz;  // Controlled_Buffer controlled_buffer_1
  assign controlled_buffer_2_out = in_2 ? d_ff_2_q : 1'bz;  // Controlled_Buffer controlled_buffer_2
  assign controlled_buffer_3_out = in_2 ? d_ff_3_q : 1'bz;  // Controlled_Buffer controlled_buffer_3
  assign controlled_buffer_4_out = in_2 ? d_ff_4_q : 1'bz;  // Controlled_Buffer controlled_buffer_4
  assign controlled_buffer_5_out = in_2 ? d_ff_5_q : 1'bz;  // Controlled_Buffer controlled_buffer_5
  assign controlled_buffer_6_out = in_2 ? d_ff_6_q : 1'bz;  // Controlled_Buffer controlled_buffer_6
  assign controlled_buffer_7_out = in_2 ? d_ff_7_q : 1'bz;  // Controlled_Buffer controlled_buffer_7
  assign controlled_buffer_8_out = in_2 ? d_ff_8_q : 1'bz;  // Controlled_Buffer controlled_buffer_8
  assign controlled_buffer_1_out = in_11 ? d_ff_9_q : 1'bz;  // Controlled_Buffer controlled_buffer_9
  assign controlled_buffer_2_out = in_11 ? d_ff_10_q : 1'bz;  // Controlled_Buffer controlled_buffer_10
  assign controlled_buffer_3_out = in_11 ? d_ff_11_q : 1'bz;  // Controlled_Buffer controlled_buffer_11
  assign controlled_buffer_4_out = in_11 ? d_ff_12_q : 1'bz;  // Controlled_Buffer controlled_buffer_12
  assign controlled_buffer_5_out = in_11 ? d_ff_13_q : 1'bz;  // Controlled_Buffer controlled_buffer_13
  assign controlled_buffer_6_out = in_11 ? d_ff_14_q : 1'bz;  // Controlled_Buffer controlled_buffer_14
  assign controlled_buffer_7_out = in_11 ? d_ff_15_q : 1'bz;  // Controlled_Buffer controlled_buffer_15
  assign controlled_buffer_8_out = in_11 ? d_ff_16_q : 1'bz;  // Controlled_Buffer controlled_buffer_16
  assign controlled_buffer_1_out = in_20 ? d_ff_17_q : 1'bz;  // Controlled_Buffer controlled_buffer_17
  assign controlled_buffer_2_out = in_20 ? d_ff_18_q : 1'bz;  // Controlled_Buffer controlled_buffer_18
  assign controlled_buffer_3_out = in_20 ? d_ff_19_q : 1'bz;  // Controlled_Buffer controlled_buffer_19
  assign controlled_buffer_4_out = in_20 ? d_ff_20_q : 1'bz;  // Controlled_Buffer controlled_buffer_20
  assign controlled_buffer_5_out = in_20 ? d_ff_21_q : 1'bz;  // Controlled_Buffer controlled_buffer_21
  assign controlled_buffer_6_out = in_20 ? d_ff_22_q : 1'bz;  // Controlled_Buffer controlled_buffer_22
  assign controlled_buffer_7_out = in_20 ? d_ff_23_q : 1'bz;  // Controlled_Buffer controlled_buffer_23
  assign controlled_buffer_8_out = in_20 ? d_ff_24_q : 1'bz;  // Controlled_Buffer controlled_buffer_24
  LED led_1 (.in(controlled_buffer_1_out));
  LED led_2 (.in(controlled_buffer_2_out));
  LED led_3 (.in(controlled_buffer_3_out));
  LED led_4 (.in(controlled_buffer_4_out));
  LED led_5 (.in(controlled_buffer_5_out));
  LED led_6 (.in(controlled_buffer_6_out));
  LED led_7 (.in(controlled_buffer_7_out));
  LED led_8 (.in(controlled_buffer_8_out));
endmodule
